// Logisim project SIMULATION.circ as structural Verilog: 1 circuit, main circuit main
module main (
  input  ROCK_01,
  input  PAPER_01,
  input  SCISSOR_01,
  input  ROCK_02,
  input  PAPER_02,
  input  SCISSOR_02,
  output out_7,
  output out_8,
  output LED_05
);

  wire and_1_out, and_2_out, and_3_out, and_4_out, and_5_out, and_6_out, not_1_out, not_2_out, not_3_out,
       or_1_out, or_2_out;

  and and_1 (and_1_out, ROCK_01, SCISSOR_02);
  and and_2 (and_2_out, ROCK_02, PAPER_01);
  and and_3 (and_3_out, SCISSOR_01, PAPER_02);
  and and_4 (and_4_out, SCISSOR_01, ROCK_02);
  and and_5 (and_5_out, ROCK_01, PAPER_02);
  and and_6 (and_6_out, PAPER_01, SCISSOR_02);
  or or_1 (or_1_out, and_1_out, and_2_out);
  or or_2 (or_2_out, and_4_out, and_5_out);
  or or_3 (out_7, or_1_out, and_3_out);
  or or_4 (LED_05, or_2_out, and_6_out);
  LED led_1 (.in(out_7));
  LED led_2 (.in(out_8));
  nor nor_1 (out_8, out_7, LED_05);
  LED led_3 (.in(LED_05));
  not not_1 (not_1_out, out_8);
  not not_2 (not_2_out, out_7);
  LED led_4 (.in(not_1_out));
  not not_3 (not_3_out, LED_05);
  LED led_5 (.in(not_2_out));
  LED led_6 (.in(not_3_out));

  // Notes on the sheet:
  //   PLAYER 01
  //   PLAYER 02
  //   AND 01
  //   AND 02
  //   AND 03
  //   AND 04
  //   AND 05
  //   AND 06
  //   OR 01
  //   LED INDICATES???
  //   *)RED INDICATES LOSING
  //   *)GREEN INDICATES WINNING
  //   *)YELLOW INDICATES IF NOT TIED
  //   *)BLUE INDICATES "GAME TIED"
  //   OR 03
  //   OR 02
  //   OR 04
  //   MUHAMMAD UMAR 19B-136-CS
  //   UMAIR ULLAH KHAN 19B-095-CS
  //   SYED MUHAMMAD ZAID 19B-140-CS
  //   USMAN AHMED KHAN 19B-072-CS
  //   GLOWS GREEN ONLY IF THE PLAYER ONE WINS
  //   NOR 01
  //   "ROCK PAPER AND SCISSOR SIMULATION"
  //   LED 01
  //   LED 03
  //   OUTPUT OF PLAYER 01
  //   OUTPUT OF GAME IF TIED
  //   GLOWS GREEN ONLY IF THE PLAYER TWO WINS
  //   OUTPUT OF PLAYER 02
  //   NOT 01
  //   GLOWS BLUE ONLY IF GAME TIED
  //   NOT 02
  //   NOT 03
  //   **RULES OF PLAYING**
  //   1.MULTIPLAYER GAME
  //   *EVERY PLAYER SHOULD GIVE ONE INPUT
  //   *EVERY PLAYER SHOULD NOT GIVE MORE THAN ONE INPUT
  //   LED 02
  //   GLOWS RED IF PLAYEER ONE LOSES
  //   LED 04
  //   LED 06
  //   GLOWS RED IF PLAYER TWO LOSES
  //   GLOWS YELLOW IF THE GAME IS NOT TIED
endmodule
